// Logisim project 4-bit full adder.circ as structural Verilog: 5 circuits, main circuit 4-bit full adder
// 4-Bit Adder
module _4_bit_full_adder (
  input  Cin,
  input  A1,
  input  B1,
  input  A2,
  input  B2,
  input  A3,
  input  B3,
  input  A4,
  input  B4,
  output S1,
  output S2,
  output S3,
  output S4,
  output Cout
);

  wire and_1_out, and_2_out, and_3_out, and_4_out, and_5_out, and_6_out, and_7_out, and_8_out, or_1_out,
       or_2_out, or_3_out, xor_1_out, xor_3_out, xor_5_out, xor_7_out;

  Pull_Resistor pull_resistor_1 (.node(Cin));
  xor xor_1 (xor_1_out, A1, B1);
  xor xor_2 (S1, xor_1_out, Cin);
  and and_1 (and_1_out, Cin, xor_1_out);
  or or_1 (or_1_out, and_1_out, and_2_out);
  and and_2 (and_2_out, B1, A1);
  xor xor_3 (xor_3_out, A2, B2);
  xor xor_4 (S2, xor_3_out, or_1_out);
  and and_3 (and_3_out, or_1_out, xor_3_out);
  or or_2 (or_2_out, and_3_out, and_4_out);
  and and_4 (and_4_out, B2, A2);
  xor xor_5 (xor_5_out, A3, B3);
  xor xor_6 (S3, xor_5_out, or_2_out);
  and and_5 (and_5_out, or_2_out, xor_5_out);
  or or_3 (or_3_out, and_5_out, and_6_out);
  and and_6 (and_6_out, B3, A3);
  xor xor_7 (xor_7_out, A4, B4);
  xor xor_8 (S4, xor_7_out, or_3_out);
  and and_7 (and_7_out, or_3_out, xor_7_out);
  or or_4 (Cout, and_7_out, and_8_out);
  and and_8 (and_8_out, B4, A4);
endmodule

// BCD
module BCD_7_segment_Decoder (
  input  A,
  input  B,
  input  C,
  input  D,
  input  BLANKING,
  output a_2,
  output b_2,
  output c_2,
  output d_2,
  output e,
  output f,
  output g
);

  wire and_1_out, and_2_out, and_3_out, and_4_out, and_5_out, and_6_out, and_7_out, and_8_out, and_9_out,
       and_10_out, and_11_out, and_12_out, and_13_out, and_14_out, and_15_out, and_16_out, and_17_out,
       buffer_1_out, buffer_2_out, nand_1_out, nand_2_out, nand_3_out, nand_4_out, not_1_out, not_2_out,
       not_3_out, not_4_out;

  Pull_Resistor pull_resistor_1 (.node(A));
  Pull_Resistor pull_resistor_2 (.node(B));
  Pull_Resistor pull_resistor_3 (.node(C));
  Pull_Resistor pull_resistor_4 (.node(D));
  Pull_Resistor #(.pull(1)) pull_resistor_5 (.node(BLANKING));
  not not_1 (not_1_out, A);
  nand nand_1 (nand_1_out, not_1_out, buffer_1_out);
  not not_2 (not_2_out, B);
  nand nand_2 (nand_2_out, not_2_out, buffer_1_out);
  not not_3 (not_3_out, C);
  nand nand_3 (nand_3_out, not_3_out, buffer_1_out);
  not not_4 (not_4_out, D);
  nand nand_4 (nand_4_out, not_4_out, buffer_1_out);
  buf buffer_1 (buffer_1_out, BLANKING);
  and and_1 (and_1_out, nand_2_out, nand_4_out);
  nor nor_1 (a_2, and_1_out, and_2_out, and_3_out);
  and and_2 (and_2_out, not_1_out, nand_3_out);
  and and_3 (and_3_out, nand_1_out, not_2_out, not_3_out, not_4_out);
  and and_4 (and_4_out, nand_2_out, nand_4_out);
  and and_5 (and_5_out, nand_1_out, not_2_out, nand_3_out);
  nor nor_2 (b_2, and_4_out, and_5_out, and_6_out);
  and and_6 (and_6_out, not_1_out, nand_2_out, nand_3_out);
  and and_7 (and_7_out, nand_3_out, nand_4_out);
  nor nor_3 (c_2, and_7_out, and_8_out);
  and and_8 (and_8_out, not_1_out, nand_2_out, not_3_out);
  and and_9 (and_9_out, nand_1_out, not_2_out, not_3_out);
  nor nor_4 (d_2, and_9_out, and_10_out, and_11_out);
  and and_10 (and_10_out, not_1_out, not_2_out, nand_3_out);
  and and_11 (and_11_out, nand_1_out, nand_2_out, nand_3_out);
  buf buffer_2 (buffer_2_out, nand_1_out);
  nor nor_5 (e, buffer_2_out, and_12_out);
  and and_12 (and_12_out, not_2_out, nand_3_out);
  and and_13 (and_13_out, nand_1_out, nand_2_out);
  and and_14 (and_14_out, nand_2_out, not_3_out);
  nor nor_6 (f, and_13_out, and_14_out, and_15_out);
  and and_15 (and_15_out, nand_1_out, not_3_out, not_4_out);
  and and_16 (and_16_out, nand_1_out, nand_2_out, nand_3_out);
  nor nor_7 (g, and_16_out, and_17_out);
  and and_17 (and_17_out, not_2_out, not_3_out, not_4_out);
  _7_Segment_Display u_7_segment_display_1 (.g(g), .f(f), .a(a_2), .b(b_2), .e(e), .d(d_2), .c(c_2));  // open: dp
endmodule

module main (
);

  wire bcd_7_segment_decoder_1_a_2, bcd_7_segment_decoder_1_b_2, bcd_7_segment_decoder_1_c_2,
       bcd_7_segment_decoder_1_d_2, bcd_7_segment_decoder_1_e, bcd_7_segment_decoder_1_f,
       bcd_7_segment_decoder_1_g, bcd_7_segment_decoder_2_a_2, bcd_7_segment_decoder_2_b_2,
       bcd_7_segment_decoder_2_c_2, bcd_7_segment_decoder_2_d_2, bcd_7_segment_decoder_2_e,
       bcd_7_segment_decoder_2_f, bcd_7_segment_decoder_2_g, bcd_7_segment_decoder_3_a_2,
       bcd_7_segment_decoder_3_b_2, bcd_7_segment_decoder_3_c_2, bcd_7_segment_decoder_3_d_2,
       bcd_7_segment_decoder_3_e, bcd_7_segment_decoder_3_f, bcd_7_segment_decoder_3_g,
       bcd_7_segment_decoder_4_a_2, bcd_7_segment_decoder_4_b_2, bcd_7_segment_decoder_4_c_2,
       bcd_7_segment_decoder_4_d_2, bcd_7_segment_decoder_4_e, bcd_7_segment_decoder_4_f,
       bcd_7_segment_decoder_4_g, button_1_out, button_2_out, button_3_out, button_4_out, button_5_out,
       button_6_out, button_7_out, button_8_out, n4_bit_full_adder_1_cout, n4_bit_full_adder_1_s1,
       n4_bit_full_adder_1_s2, n4_bit_full_adder_1_s3, n4_bit_full_adder_1_s4, t_ff_1_q, t_ff_2_q, t_ff_3_q,
       t_ff_4_q, t_ff_5_q, t_ff_6_q, t_ff_7_q, t_ff_8_q;

  Button button_1 (.out(button_1_out));
  Button button_2 (.out(button_2_out));
  Button button_3 (.out(button_3_out));
  Button button_4 (.out(button_4_out));
  Button button_5 (.out(button_5_out));
  Button button_6 (.out(button_6_out));
  Button button_7 (.out(button_7_out));
  Button button_8 (.out(button_8_out));
  T_Flip_Flop t_ff_1 (.clk(button_1_out), .T(button_1_out), .Q(t_ff_1_q));  // open: Qn, preset, reset, en
  T_Flip_Flop t_ff_2 (.clk(button_2_out), .T(button_2_out), .Q(t_ff_2_q));  // open: Qn, preset, reset, en
  T_Flip_Flop t_ff_3 (.clk(button_3_out), .T(button_3_out), .Q(t_ff_3_q));  // open: Qn, preset, reset, en
  T_Flip_Flop t_ff_4 (.clk(button_4_out), .T(button_4_out), .Q(t_ff_4_q));  // open: Qn, preset, reset, en
  T_Flip_Flop t_ff_5 (.clk(button_5_out), .T(button_5_out), .Q(t_ff_5_q));  // open: Qn, preset, reset, en
  T_Flip_Flop t_ff_6 (.clk(button_6_out), .T(button_6_out), .Q(t_ff_6_q));  // open: Qn, preset, reset, en
  T_Flip_Flop t_ff_7 (.clk(button_7_out), .T(button_7_out), .Q(t_ff_7_q));  // open: Qn, preset, reset, en
  T_Flip_Flop t_ff_8 (.clk(button_8_out), .T(button_8_out), .Q(t_ff_8_q));  // open: Qn, preset, reset, en
  BCD_7_segment_Decoder bcd_7_segment_decoder_1 (
    .A(t_ff_1_q), .B(t_ff_2_q), .C(t_ff_3_q), .D(t_ff_4_q), .a_2(bcd_7_segment_decoder_1_a_2),
    .b_2(bcd_7_segment_decoder_1_b_2), .c_2(bcd_7_segment_decoder_1_c_2), .d_2(bcd_7_segment_decoder_1_d_2),
    .e(bcd_7_segment_decoder_1_e), .f(bcd_7_segment_decoder_1_f), .g(bcd_7_segment_decoder_1_g));  // open: BLANKING
  BCD_7_segment_Decoder bcd_7_segment_decoder_2 (
    .A(t_ff_5_q), .B(t_ff_6_q), .C(t_ff_7_q), .D(t_ff_8_q), .a_2(bcd_7_segment_decoder_2_a_2),
    .b_2(bcd_7_segment_decoder_2_b_2), .c_2(bcd_7_segment_decoder_2_c_2), .d_2(bcd_7_segment_decoder_2_d_2),
    .e(bcd_7_segment_decoder_2_e), .f(bcd_7_segment_decoder_2_f), .g(bcd_7_segment_decoder_2_g));  // open: BLANKING
  _7_Segment_Display u_7_segment_display_1 (
    .g(bcd_7_segment_decoder_1_g), .f(bcd_7_segment_decoder_1_f), .a(bcd_7_segment_decoder_1_a_2),
    .b(bcd_7_segment_decoder_1_b_2), .e(bcd_7_segment_decoder_1_e), .d(bcd_7_segment_decoder_1_d_2),
    .c(bcd_7_segment_decoder_1_c_2));  // open: dp
  _7_Segment_Display u_7_segment_display_2 (
    .g(bcd_7_segment_decoder_2_g), .f(bcd_7_segment_decoder_2_f), .a(bcd_7_segment_decoder_2_a_2),
    .b(bcd_7_segment_decoder_2_b_2), .e(bcd_7_segment_decoder_2_e), .d(bcd_7_segment_decoder_2_d_2),
    .c(bcd_7_segment_decoder_2_c_2));  // open: dp
  BCD_7_segment_Decoder bcd_7_segment_decoder_3 (
    .A(n4_bit_full_adder_1_s1), .B(n4_bit_full_adder_1_s2), .C(n4_bit_full_adder_1_s3),
    .D(n4_bit_full_adder_1_s4), .a_2(bcd_7_segment_decoder_3_a_2), .b_2(bcd_7_segment_decoder_3_b_2),
    .c_2(bcd_7_segment_decoder_3_c_2), .d_2(bcd_7_segment_decoder_3_d_2), .e(bcd_7_segment_decoder_3_e),
    .f(bcd_7_segment_decoder_3_f), .g(bcd_7_segment_decoder_3_g));  // open: BLANKING
  _4_bit_full_adder u_4_bit_full_adder_1 (
    .A1(t_ff_1_q), .B1(t_ff_5_q), .A2(t_ff_2_q), .B2(t_ff_6_q), .A3(t_ff_3_q), .B3(t_ff_7_q), .A4(t_ff_4_q),
    .B4(t_ff_8_q), .Cout(n4_bit_full_adder_1_cout), .S1(n4_bit_full_adder_1_s1), .S2(n4_bit_full_adder_1_s2),
    .S3(n4_bit_full_adder_1_s3), .S4(n4_bit_full_adder_1_s4));  // open: Cin
  BCD_7_segment_Decoder bcd_7_segment_decoder_4 (
    .A(n4_bit_full_adder_1_cout), .a_2(bcd_7_segment_decoder_4_a_2), .b_2(bcd_7_segment_decoder_4_b_2),
    .c_2(bcd_7_segment_decoder_4_c_2), .d_2(bcd_7_segment_decoder_4_d_2), .e(bcd_7_segment_decoder_4_e),
    .f(bcd_7_segment_decoder_4_f), .g(bcd_7_segment_decoder_4_g));  // open: B, C, D, BLANKING
  _7_Segment_Display u_7_segment_display_3 (
    .g(bcd_7_segment_decoder_3_g), .f(bcd_7_segment_decoder_3_f), .a(bcd_7_segment_decoder_3_a_2),
    .b(bcd_7_segment_decoder_3_b_2), .e(bcd_7_segment_decoder_3_e), .d(bcd_7_segment_decoder_3_d_2),
    .c(bcd_7_segment_decoder_3_c_2));  // open: dp
  _7_Segment_Display u_7_segment_display_4 (
    .g(bcd_7_segment_decoder_4_g), .f(bcd_7_segment_decoder_4_f), .a(bcd_7_segment_decoder_4_a_2),
    .b(bcd_7_segment_decoder_4_b_2), .e(bcd_7_segment_decoder_4_e), .d(bcd_7_segment_decoder_4_d_2),
    .c(bcd_7_segment_decoder_4_c_2));  // open: dp
endmodule

module dumbshit (
);

  wire nand_1_out, nand_2_out, nand_3_out, nand_4_out, nand_5_out, not_1_out, not_2_out, undriven,
       undriven_2, undriven_3, xor_1_out, xor_2_out;

  xor xor_1 (xor_1_out, undriven, undriven_2);
  nand nand_1 (nand_1_out, undriven_3, xor_1_out);
  nand nand_2 (nand_2_out, undriven_2, undriven);
  xor xor_2 (xor_2_out, xor_1_out, undriven_3);
  not not_1 (not_1_out, nand_1_out);
  not not_2 (not_2_out, nand_2_out);
  nand nand_3 (nand_3_out, not_1_out, not_1_out);
  nand nand_4 (nand_4_out, not_2_out, not_2_out);
  nand nand_5 (nand_5_out, nand_3_out, nand_4_out);
endmodule

module SR_Latch (
);

  wire button_1_out, button_2_out, nand_1_out, nand_2_out, not_1_out, not_2_out;

  Button button_1 (.out(button_1_out));
  Button button_2 (.out(button_2_out));
  not not_1 (not_1_out, button_1_out);
  not not_2 (not_2_out, button_2_out);
  nand nand_1 (nand_1_out, not_1_out, nand_2_out);
  nand nand_2 (nand_2_out, nand_1_out, not_2_out);
  LED led_1 (.in(nand_1_out));
  LED led_2 (.in(nand_2_out));
endmodule
